// Logisim project tp_1.circ as structural Verilog
module portenot (
  input  in_1,
  output out_2
);

  Pull_Resistor #(.pull(1)) pull_resistor_1 (.node(out_2));
  Transistor #(.\type ("n")) transistor_1 (.in(1'b0), .out(out_2), .gate(in_1));
endmodule

module porteNOR (
  input  in_1,
  input  in_2,
  output out_3
);

  Pull_Resistor #(.pull(1)) pull_resistor_1 (.node(out_3));
  Transistor #(.\type ("n")) transistor_1 (.in(1'b0), .out(out_3), .gate(in_1));
  Transistor #(.\type ("n")) transistor_2 (.in(1'b0), .out(out_3), .gate(in_2));
endmodule

module porteNAND (
  input  in_1,
  input  in_2,
  output out_3
);

  wire transistor_2_out;

  Pull_Resistor #(.pull(1)) pull_resistor_1 (.node(out_3));
  Transistor #(.\type ("n")) transistor_1 (.in(transistor_2_out), .out(out_3), .gate(in_1));
  Transistor #(.\type ("n")) transistor_2 (.in(1'b0), .out(transistor_2_out), .gate(in_2));
endmodule

module porteXOR (
  input  za,
  input  zb,
  input  a,
  input  b,
  output out_5
);

  wire and_1_out, and_2_out, not_1_out, not_2_out, not_3_out, not_4_out, or_1_out, transistor_1_out,
       transistor_2_out, transistor_3_out, transistor_4_out, transistor_5_out, transistor_6_out,
       transistor_7_out, transistor_8_out, undriven;

  not not_1 (not_1_out, transistor_1_out);
  Transistor #(.\type ("n")) transistor_1 (.in(1'b0), .out(transistor_1_out), .gate(za));
  Transistor #(.\type ("n")) transistor_2 (.in(1'b0), .out(transistor_2_out), .gate(zb));
  not not_2 (not_2_out, zb);
  Transistor #(.\type ("n")) transistor_3 (.in(1'b0), .out(transistor_3_out), .gate(a));
  Transistor #(.\type ("n")) transistor_4 (.in(1'b0), .out(transistor_4_out), .gate(b));
  and and_1 (and_1_out, not_1_out, transistor_2_out);
  and and_2 (and_2_out, za, not_2_out);
  Transistor #(.\type ("n")) transistor_5 (.in(1'b0), .out(transistor_5_out), .gate(transistor_3_out));
  Transistor #(.\type ("n")) transistor_6 (.in(b), .out(transistor_6_out), .gate(b));
  not not_3 (not_3_out, and_1_out);
  not not_4 (not_4_out, and_2_out);
  Transistor #(.\type ("n")) transistor_7 (.in(undriven), .out(transistor_7_out), .gate(transistor_5_out));
  Transistor #(.\type ("n")) transistor_8 (.in(1'b0), .out(transistor_8_out), .gate(transistor_7_out));
  Transistor #(.\type ("n")) transistor_9 (.in(undriven), .out(transistor_7_out), .gate(transistor_4_out));
  or or_1 (or_1_out, not_3_out, not_4_out);
  not not_5 (out_5, or_1_out);
  Pull_Resistor #(.pull(1)) pull_resistor_1 (.node(out_5));
  // also tied to GND on the sheet: {a, b}

  // Notes on the sheet:
  //   a
  //   b
  //   a
  //   b
endmodule

module NmosNOT (
  input  in_1,
  output out_2
);

  Transistor transistor_1 (.in(1'b1), .out(out_2), .gate(in_1));
  Pull_Resistor pull_resistor_1 (.node(out_2));
endmodule

module cmosex5 (
  input  a,
  input  b,
  input  d,
  input  c,
  output out_5
);

  wire pull_resistor_1_node, pull_resistor_2_node, transistor_2_out, undriven;

  Pull_Resistor #(.pull(1)) pull_resistor_1 (.node(pull_resistor_1_node));
  // Probe on pull_resistor_1_node
  Transistor #(.\type ("n"), .gate("br")) transistor_1 (.in(transistor_2_out), .out(pull_resistor_1_node), .gate(b));
  Transistor #(.\type ("n")) transistor_2 (.in(1'b0), .out(transistor_2_out), .gate(a));
  // Probe on undriven
  Pull_Resistor #(.pull(1)) pull_resistor_2 (.node(pull_resistor_2_node));
  Transistor #(.\type ("n")) transistor_3 (.in(1'b0), .out(pull_resistor_2_node), .gate(pull_resistor_1_node));
  Transistor #(.\type ("n"), .gate("br")) transistor_4 (.in(1'b0), .out(pull_resistor_2_node), .gate(c));
  Pull_Resistor #(.pull(1)) pull_resistor_3 (.node(pull_resistor_2_node));
  Pull_Resistor #(.pull(1)) pull_resistor_4 (.node(pull_resistor_2_node));
  Transistor #(.\type ("n"), .gate("br")) transistor_5 (.in(1'b0), .out(pull_resistor_2_node), .gate(d));
  Transistor #(.\type ("n")) transistor_6 (.in(1'b0), .out(out_5), .gate(pull_resistor_2_node));
  Pull_Resistor #(.pull(1)) pull_resistor_5 (.node(out_5));

  // Notes on the sheet:
  //   pb avec le a.b
endmodule
